// Logisim project arch.circ as structural Verilog
module PC (
  input  CLK,
  input  CLR,
  output [3:0] PC0,
  output [3:0] PC1
);

  wire d_ff_1_q;
  wire [3:0] adder_1_out, adder_2_out, multiplexer_1_out, multiplexer_2_out;

  D_Flip_Flop d_ff_1 (.clk(CLK), .Q(d_ff_1_q), .preset(CLK), .reset(CLR));  // open: D, Qn
  Multiplexer #(.width(4)) multiplexer_1 (.in0(4'b0000), .in1(adder_1_out), .out(multiplexer_1_out), .sel(d_ff_1_q));
  Multiplexer #(.width(4)) multiplexer_2 (.in0(4'b0001), .in1(adder_2_out), .out(multiplexer_2_out), .sel(d_ff_1_q));
  Counter #(.max('hf), .ongoal("stay"), .width(4)) counter_1 (
    .load(1'b1), .D(multiplexer_1_out), .Q(PC0), .clk(CLK), .clr(CLR));  // open: count, carry, up
  Counter #(.max('hf), .ongoal("stay"), .width(4)) counter_2 (
    .load(1'b1), .D(multiplexer_2_out), .Q(PC1), .clk(CLK), .clr(CLR));  // open: count, carry, up
  Adder #(.width(4)) adder_1 (.a(4'b0010), .b(PC0), .out(adder_1_out));  // open: cin, cout
  Adder #(.width(4)) adder_2 (.a(4'b0010), .b(PC1), .out(adder_2_out));  // open: cin, cout
endmodule
